# Fritzing sketch FlashEspWithArduino (saved by Fritzing 0.9.3b)
breadboards: 1

parts:
  Arduino_Uno = Arduino Uno (Rev3) - ICSP
  C2 = Electrolytic Capacitor [capacitance=10µF package="100 mil [THT, electrolytic]"]
  U2 = ESP8266 WiFi Module [part_number=ESP8266]
  Program = Momentary Switch [package=ksa_sealed_tac_switch]
  R1 = Resistor [tolerance=±5% resistance=10k package=THT]
  R2 = Resistor [tolerance=±5% resistance=10k package=THT]
  R3 = Resistor [tolerance=±5% resistance=10k package=THT]
  R4 = Resistor [tolerance=±5% resistance=470 package=THT]
  R5 = Resistor [tolerance=±5% resistance=10k package=THT]
  R6 = Resistor [tolerance=±5% resistance=2.2k package=THT]
  C3 = Ceramic Capacitor [capacitance=100nF package="100 mil [THT, multilayer]"]
  IC1 = V_REG_LD1117VXX [package=78xxl]
  Reset = Momentary Switch [package=ksa_sealed_tac_switch]

nets:
  5V: Arduino_Uno.5V, C3.1, IC1.IN
  GND: Arduino_Uno.RESET, Arduino_Uno.GND, C2.-, U2.GND, R2.Pin_1, R4.Pin_1, R6.Pin_0, C3.0, IC1.GND, Reset.1
  RX: Arduino_Uno.D0/RX, U2.RXD, R6.Pin_1
  TX: Arduino_Uno.D1/TX, U2.TXD
  3.3V: C2.+, U2.VCC, R1.Pin_0, R3.Pin_0, R5.Pin_0, IC1.OUT
  N1: U2.GPIO_0, Program.3, R5.Pin_1
  N2: U2.CH_PD, R3.Pin_1
  N3: U2.GPIO_15, R2.Pin_0
  N4: U2.REST, R1.Pin_1, Reset.3
  N5: Program.1, R4.Pin_0
