# Fritzing sketch Tempea-esp Schematic (saved by Fritzing 0.9.3b)
circuit board: 8.46667cm x 5.64444cm
breadboards: 1

parts:
  WeMos_D1_Mini1 = WeMos D1 Mini
  DS1 = DS18B20 1-Wire Temperature Sensor [part_number=DS18B20]
  R1 = Resistor [tolerance=±5% resistance=4.7k package=THT]

nets:
  3V3: WeMos_D1_Mini1.3V3, WeMos_D1_Mini1.D1, DS1.DQ, DS1.VDD, R1.Pin_0, R1.Pin_1
  N1: WeMos_D1_Mini1.D0, WeMos_D1_Mini1.RST
  N2: WeMos_D1_Mini1.G, DS1.GND
